// Logisim project Lab 4 Final.circ as structural Verilog: 16 circuits, main circuit Main
module Main (
);

  wire alu_1_overflow, ALU_Zero, ALU_Zero_Out, ALUSrcB, and_1_out, Branch, Clock, Control_Write, Do_Branch,
       Forward_A_MEM, Forward_A_WB, Forward_B_MEM, Forward_B_WB, hazard_detection_1_pcwrite, ID_EX_MemRead,
       IF_ID_Write, J, JR_Squash, MemRead, MemWr, not_1_out, not_2_out, not_3_out, not_4_out, not_5_out,
       or_2_out, PCWrite, register_3_q, RegWrite, RegWrite_EX_MEM, Squash, Uncond_squash, undriven;
  wire [0:0] PCSrc;
  wire [1:0] aluctl_1_jr, JR_Mux, mem_wb_1_memtoreg, or_1_out, or_4_out, RegDst, To_Mem_WB;
  wire [2:0] ALUOp, multiplexer_7_out, WB, WBOUT;
  wire [3:0] aluctl_1_toalu;
  wire [4:0] Inst_15_11, Inst_15_11__EX, Inst_20_16, Inst_20_16__EX, Inst_25_21, Inst_25_21__EX,
       Instruction_Out, MEM, MEMOUT, multiplexer_6_out, multiplexer_8_out, Reg_Address_Out;
  wire [5:0] EX, Inst_31_26;
  wire [10:0] IR_Out;
  wire [27:0] PC_4_OUT;
  wire [31:0] A_Out, adder_1_out, adder_2_out, ALU_Out, ALU_Result_Out, B_Out, Branch_Target_Address,
       im_1_read_data, Inst_25_0, Inst_25_0__EX_MEM, mem_wb_1_read_data_out, mem_wb_1_write_address_out,
       MemData, multiplexer_1_out, multiplexer_2_out, multiplexer_3_out, multiplexer_4_out,
       multiplexer_5_out, multiplexer_9_out, PC_4_OUT_EX, PCOut, PCOut_MEM_WB, Read_Data, Reg_Write_Data,
       register_5_q, register_6_q, register_file_1_rddata1, register_file_1_rddata2, shifter_1_out,
       Sign_Extend, Sign_Extend_OUT;

  not not_1 (not_1_out, PCWrite);
  Register #(.width(32)) PC (.D(multiplexer_1_out), .en(not_1_out), .Q(PCOut), .clk(Clock));  // open: clr
  Clock clock_1 (.out(Clock));
  Multiplexer #(.select(2), .width(32), .enable("false")) multiplexer_1 (
    .in0(adder_1_out), .in1(Branch_Target_Address), .in2(Inst_25_0__EX_MEM), .in3(ALU_Out),
    .out(multiplexer_1_out), .sel(or_1_out));
  Adder #(.width(32)) adder_1 (.a(PCOut), .b(32'h4), .out(adder_1_out));  // open: cin, cout
  Multiplexer #(.select(2), .width(32), .enable("false")) multiplexer_2 (
    .in0(B_Out), .in1(Reg_Write_Data), .in2(ALU_Out), .out(multiplexer_2_out),
    .sel({Forward_B_MEM, Forward_B_WB}));  // open: in3
  Multiplexer #(.select(2), .width(32), .enable("false")) multiplexer_3 (
    .in0(A_Out), .in1(Reg_Write_Data), .in2(ALU_Out), .out(multiplexer_3_out),
    .sel({Forward_A_MEM, Forward_A_WB}));  // open: in3
  assign or_1_out = JR_Mux | {J, Do_Branch};  // OR_Gate or_1, 2 bits wide
  IM im_1 (.Read_Address(PCOut[9:2]), .Clock(Clock), .Read_Data(im_1_read_data));
  Multiplexer #(.width(32), .enable("false")) multiplexer_4 (
    .in0(im_1_read_data), .in1({32{1'b0}}), .out(multiplexer_4_out), .sel(Squash));
  not not_2 (not_2_out, IF_ID_Write);
  Hazard_Detection hazard_detection_1 (
    .MemRead(ID_EX_MemRead), .ID_EX_Register_Rt(Inst_20_16__EX), .IF_ID_RegisterRs(Inst_25_21),
    .IF_ID_RegisterRt(Inst_20_16), .PCWrite(hazard_detection_1_pcwrite), .IF_IDWrite(IF_ID_Write),
    .ControlWrite(Control_Write));
  IF_ID if_id_1 (
    .PC_4(adder_1_out), .Read_Address(multiplexer_4_out), .Clock(Clock),
    .PC_4_Out({Inst_25_0[31:28], PC_4_OUT}),
    .Read_Address_Out({Inst_31_26, Inst_25_21, Inst_20_16, Inst_15_11, IR_Out}), .IF_IDWrite(not_2_out));
  // Probe on {Inst_31_26, Inst_25_21, Inst_20_16, Inst_15_11, IR_Out}
  // Probe on multiplexer_4_out
  Multiplexer #(.width(32), .enable("false")) multiplexer_5 (
    .in0(multiplexer_2_out), .in1(Sign_Extend_OUT), .out(multiplexer_5_out), .sel(ALUSrcB));
  Shifter #(.width(32)) shifter_1 (.in(Sign_Extend_OUT), .\dist (5'b00010), .out(shifter_1_out));
  ALUCTL aluctl_1 (.Instr_5_0(Sign_Extend_OUT[5:0]), .ALUOp(ALUOp), .ToALU(aluctl_1_toalu), .JR(aluctl_1_jr));
  ALU alu_1 (
    .ALUCtl(aluctl_1_toalu), .A(multiplexer_3_out), .B(multiplexer_5_out), .ALUResult(ALU_Result_Out),
    .Zero(ALU_Zero), .Overflow(alu_1_overflow), .Shamt(Sign_Extend_OUT[10:6]));
  not not_3 (not_3_out, Do_Branch);
  not not_4 (not_4_out, or_2_out);
  Register #(.width(2)) register_1 (.D(aluctl_1_jr), .Q(JR_Mux), .clk(Clock));  // open: en, clr
  and and_1 (and_1_out, Branch, not_3_out);
  Control_Unit control_unit_1 (
    .RegDst(EX[1:0]), .ALUSrcB(EX[2]), .MemtoReg(WB[1:0]), .RegWrite(WB[2]), .MemRead(MEM[2]),
    .MemWrite(MEM[3]), .PCWriteCond(MEM[4]), .ALUOP(EX[5:3]), .Op5(Inst_31_26[5]), .Op4(Inst_31_26[4]),
    .Op3(Inst_31_26[3]), .Op2(Inst_31_26[2]), .Op1(Inst_31_26[1]), .Op0(Inst_31_26[0]), .in_7(not_4_out),
    .PCSRC(MEM[1:0]));
  or or_2 (or_2_out, Squash, Control_Write);
  Register #(.width(1)) register_2 (.D(aluctl_1_jr[1]), .Q(JR_Squash), .clk(Clock));  // open: en, clr
  or or_3 (PCWrite, and_1_out, hazard_detection_1_pcwrite);
  Adder #(.width(32)) adder_2 (.a(shifter_1_out), .b(PC_4_OUT_EX), .out(adder_2_out));  // open: cin, cout
  Register_File register_file_1 (
    .WrAddr(Reg_Address_Out), .WrData(Reg_Write_Data), .WrReg(RegWrite), .RdAddr1(Inst_25_21),
    .RdAddr2(Inst_20_16), .RdData1(register_file_1_rddata1), .RdData2(register_file_1_rddata2), .Clock(Clock));
  Multiplexer #(.select(2), .width(5), .enable("false")) multiplexer_6 (
    .in0(Inst_20_16__EX), .in1(Inst_15_11__EX), .in2({5{1'b1}}), .out(multiplexer_6_out), .sel(or_4_out));  // open: in3
  assign or_4_out = JR_Mux | RegDst;  // OR_Gate or_4, 2 bits wide
  Multiplexer #(.width(3), .enable("false")) multiplexer_7 (
    .in0(WBOUT), .in1(3'b000), .out(multiplexer_7_out), .sel(Squash));
  Multiplexer #(.width(5), .enable("false")) multiplexer_8 (
    .in0({MEMOUT[4:3], ID_EX_MemRead, MEMOUT[1:0]}), .in1({5{1'b0}}), .out(multiplexer_8_out), .sel(Squash));
  Multiplexer #(.select(2), .width(32), .enable("false")) multiplexer_9 (
    .in0(B_Out), .in1(ALU_Out), .in2(Reg_Write_Data), .out(multiplexer_9_out),
    .sel({Forward_B_WB, Forward_B_MEM}));  // open: in3
  assign Sign_Extend = {{16{Inst_15_11[4]}}, {Inst_15_11, IR_Out}};  // Bit_Extender bit_extender_1
  Shifter #(.width(28)) shifter_2 (
    .in({Inst_31_26[1:0], Inst_25_21, Inst_20_16, Inst_15_11, IR_Out}), .\dist (5'b00010),
    .out(Inst_25_0[27:0]));
  EX_MEM ex_mem_1 (
    .M(multiplexer_8_out), .Add_Result(adder_2_out), .ALU_Zero(ALU_Zero), .ALU_Result(ALU_Result_Out),
    .Read_Data_2(multiplexer_9_out), .Instruction(multiplexer_6_out), .WB_Out({RegWrite_EX_MEM, To_Mem_WB}),
    .Add_Result_Out(Branch_Target_Address), .ALU_Zero_Out(ALU_Zero_Out), .ALU_Result_Out(ALU_Out),
    .Read_Data_2_Out(MemData), .Instruction_Out(Instruction_Out), .WB(multiplexer_7_out), .Clock(Clock),
    .Branch(Branch), .MemRead(MemRead), .MemWrite(MemWr), .PCSrc({J, PCSrc[0]}));
  ID_EX id_ex_1 (
    .EX(EX), .MEM(MEM), .WB(WB), .PC_4({Inst_25_0[31:28], PC_4_OUT}), .ReadData1(register_file_1_rddata1),
    .ReadData2(register_file_1_rddata2), .SignExtend(Sign_Extend), .Clock(Clock),
    .out_16({MEMOUT[4:3], ID_EX_MemRead, MEMOUT[1:0]}), .out_17(WBOUT), .PC_4_2(PC_4_OUT_EX),
    .ReadData1_2(A_Out), .ReadData2_2(B_Out), .SignExtend_2(Sign_Extend_OUT), .RegDst(RegDst), .ALUOp(ALUOp),
    .ALUSrcB(ALUSrcB), .in_8(Inst_15_11), .in_9(Inst_20_16), .out_22(Inst_15_11__EX),
    .out_23(Inst_20_16__EX), .in_10(Inst_25_21), .out_24(Inst_25_21__EX), .in_11(Inst_25_0),
    .out_25(Inst_25_0__EX_MEM));
  Forwarding_Unit forwarding_unit_1 (
    .RegWrite_Mem(RegWrite_EX_MEM), .RegWrite_WB(RegWrite), .rd_MEM(Instruction_Out),
    .rd_WB(Reg_Address_Out), .rd_EX(Inst_20_16__EX), .rs_EX(Inst_25_21__EX), .Forwad_B_MEM(Forward_B_MEM),
    .Forward_B_WB(Forward_B_WB), .Forward_A_Mem(Forward_A_MEM), .Forward_A_WB(Forward_A_WB));
  or or_5 (Squash, Do_Branch, Uncond_squash, JR_Squash);
  and and_2 (Do_Branch, Branch, ALU_Zero_Out);
  DM dm_1 (
    .Address(ALU_Out[7:0]), .Write_Data(MemData), .MemWrite(MemWr), .Clock(Clock), .MemRead(MemRead),
    .Read_Data(Read_Data));
  // Probe on PCOut
  // Probe on nothing
  // Probe on nothing
  // Probe on nothing
  // Probe on nothing
  // Probe on nothing
  // Probe on Reg_Address_Out
  // Probe on Reg_Write_Data
  // Probe on MemWr
  // Probe on MemData
  Register #(.width(1)) register_3 (.D(MEM[1]), .Q(register_3_q), .clk(Clock));  // open: en, clr
  Register #(.width(1)) register_4 (.D(register_3_q), .Q(Uncond_squash), .clk(Clock));  // open: en, clr
  MEM_WB mem_wb_1 (
    .Read_Data(Read_Data), .Write_Address(ALU_Out), .Reg_Address(Instruction_Out), .Clock(Clock),
    .Read_Data_Out(mem_wb_1_read_data_out), .Write_Address_Out(mem_wb_1_write_address_out),
    .Reg_AddressOut(Reg_Address_Out), .WB({RegWrite_EX_MEM, To_Mem_WB}), .RegWrite(RegWrite),
    .MemToReg(mem_wb_1_memtoreg));
  Register #(.width(32)) register_5 (.D({Inst_25_0[31:28], PC_4_OUT}), .Q(register_5_q), .clk(Clock));  // open: en, clr
  Multiplexer #(.select(2), .width(32), .enable("false")) multiplexer_10 (
    .in0(mem_wb_1_write_address_out), .in1(mem_wb_1_read_data_out), .in2(PCOut_MEM_WB), .out(Reg_Write_Data),
    .sel(mem_wb_1_memtoreg));  // open: in3
  Register #(.width(32)) register_6 (.D(register_5_q), .Q(register_6_q), .clk(Clock));  // open: en, clr
  Register #(.width(32)) register_7 (.D(register_6_q), .Q(PCOut_MEM_WB), .clk(Clock));  // open: en, clr
  not not_5 (not_5_out, undriven);

  // Other names for the same wires on the sheet: IR_Out[31:11] = {Inst_31_26, Inst_25_21, Inst_20_16, Inst_15_11};
  //   PC_4_OUT[31:28] = Inst_25_0[31:28]; Uncond_J = MEM[1]; MEMOUT[2] = ID_EX_MemRead; MemWrite = MemWr;
  //   PCSrc[1] = J; Read_Data_2_Out[31:0] = MemData; To_Mem_WB[2] = RegWrite_EX_MEM; WrAddr[4:0] = Reg_Address_Out;
  //   WriteData[31:0] = Reg_Write_Data

  // Notes on the sheet:
  //   Source Reg
  //   Opcodes
  //   Branch taken, JR, J, and JAL all require squashing
  //   IF ID EX must be squashed
  //   Carries PC+4 to MEM/WB
  //   Uncond J is high during Decode state, squash occurs in MEM state
endmodule

module ALU (
  input  [3:0] ALUCtl,
  input  [31:0] A,
  input  [31:0] B,
  input  [4:0] Shamt,
  output [31:0] ALUResult,
  output Zero,
  output Overflow
);

  wire comparator_1_lt, comparator_2_lt, comparator_3_eq, comparator_4_eq, or_2_out;
  wire [31:0] ADD, AND, NOR, OR, SLL, SLT, SLTU, SRL, SUB, XOR;

  assign XOR = A ^ B;  // XOR_Gate xor_1, 32 bits wide
  Adder #(.width(32)) adder_1 (.a(A), .b(B), .out(ADD));  // open: cin, cout
  Subtractor #(.width(32)) subtractor_1 (.a(A), .b(B), .out(SUB));  // open: bin, bout
  assign AND = A & B;  // AND_Gate and_1, 32 bits wide
  assign OR = A | B;  // OR_Gate or_1, 32 bits wide
  assign NOR = ~(A | B);  // NOR_Gate nor_1, 32 bits wide
  Comparator #(.width(32)) comparator_1 (.a(A), .b(B), .lt(comparator_1_lt));  // open: gt, eq
  assign SLT = {{31{1'b0}}, comparator_1_lt};  // Bit_Extender bit_extender_1
  Shifter #(.width(32)) shifter_1 (.in(B), .\dist (Shamt), .out(SLL));
  Shifter #(.width(32), .shift("lr")) shifter_2 (.in(B), .\dist (Shamt), .out(SRL));
  Comparator #(.width(32), .mode("unsigned")) comparator_2 (.a(A), .b(B), .lt(comparator_2_lt));  // open: gt, eq
  assign SLTU = {{31{1'b0}}, comparator_2_lt};  // Bit_Extender bit_extender_2
  Multiplexer #(.select(4), .width(32), .enable("false")) multiplexer_1 (
    .in0(ADD), .in1(SUB), .in2(AND), .in3(OR), .in4(NOR), .in5(XOR), .in6(SLT), .in14(SLL), .in15(SRL),
    .out(ALUResult), .sel(ALUCtl));  // open: in7, in8, in9, in10, in11, in12, in13
  Comparator #(.width(4)) comparator_3 (.a(4'b0000), .b(ALUCtl), .eq(comparator_3_eq));  // open: gt, lt
  Comparator #(.width(4)) comparator_4 (.a(ALUCtl), .b(4'b0001), .eq(comparator_4_eq));  // open: gt, lt
  Overflow_Unit overflow_unit_1 (
    .Add(comparator_3_eq), .Sub(comparator_4_eq), .ASign(A[31]), .BSign(B[31]), .ResultSign(ALUResult[31]),
    .Overflow(Overflow));
  not not_1 (Zero, or_2_out);
  or or_2 (or_2_out, ALUResult[0], ALUResult[1], ALUResult[2], ALUResult[3], ALUResult[4], ALUResult[5], ALUResult[6], ALUResult[7], ALUResult[8], ALUResult[9], ALUResult[10], ALUResult[11], ALUResult[12], ALUResult[13], ALUResult[14], ALUResult[15], ALUResult[16], ALUResult[17], ALUResult[18], ALUResult[19], ALUResult[20], ALUResult[21], ALUResult[22], ALUResult[23], ALUResult[24], ALUResult[25], ALUResult[26], ALUResult[27], ALUResult[28], ALUResult[29], ALUResult[30], ALUResult[31]);

  // Other names for the same wires on the sheet: ASign = A[31]; ResultSign = ALUResult[31]; BSign = B[31]

  // Notes on the sheet:
  //   ALUCtl for ADD on top port
  //   ALUCtl for SUB on second port
endmodule

module Register_File (
  input  [4:0] WrAddr,
  input  [31:0] WrData,
  input  WrReg,
  input  [4:0] RdAddr1,
  input  [4:0] RdAddr2,
  input  Clock,
  output [31:0] RdData1,
  output [31:0] RdData2
);

  wire and_1_out, and_2_out, comparator_1_eq, comparator_2_eq, comparator_3_eq, comparator_4_eq, not_1_out,
       not_2_out, WrReg0, WrReg1, WrReg2, WrReg3, WrReg4, WrReg5, WrReg6, WrReg7, WrReg8, WrReg9, WrReg10,
       WrReg11, WrReg12, WrReg13, WrReg14, WrReg15, WrReg16, WrReg17, WrReg18, WrReg19, WrReg20, WrReg21,
       WrReg22, WrReg23, WrReg24, WrReg25, WrReg26, WrReg27, WrReg28, WrReg29, WrReg30, WrReg31;
  wire [31:0] multiplexer_1_out, multiplexer_2_out, RegData1, RegData2, RegData3, RegData4, RegData5,
       RegData6, RegData7, RegData8, RegData9, RegData10, RegData11, RegData12, RegData13, RegData14,
       RegData15, RegData16, RegData17, RegData18, RegData19, RegData20, RegData21, RegData22, RegData23,
       RegData24, RegData25, RegData26, RegData27, RegData28, RegData29, RegData30, RegData31;

  Demultiplexer #(.select(5), .enable("false")) demultiplexer_1 (
    .out0(WrReg0), .out1(WrReg1), .out2(WrReg2), .out3(WrReg3), .out4(WrReg4), .out5(WrReg5), .out6(WrReg6),
    .out7(WrReg7), .out8(WrReg8), .out9(WrReg9), .out10(WrReg10), .out11(WrReg11), .out12(WrReg12),
    .out13(WrReg13), .out14(WrReg14), .out15(WrReg15), .out16(WrReg16), .out17(WrReg17), .out18(WrReg18),
    .out19(WrReg19), .out20(WrReg20), .out21(WrReg21), .out22(WrReg22), .out23(WrReg23), .out24(WrReg24),
    .out25(WrReg25), .out26(WrReg26), .out27(WrReg27), .out28(WrReg28), .out29(WrReg29), .out30(WrReg30),
    .out31(WrReg31), .in(WrReg), .sel(WrAddr));
  // Probe on RegData4
  Register #(.width(32)) Reg4 (.D(WrData), .en(WrReg4), .Q(RegData4), .clk(Clock));  // open: clr
  // Probe on RegData8
  Register #(.width(32)) Reg8 (.D(WrData), .en(WrReg8), .Q(RegData8), .clk(Clock));  // open: clr
  // Probe on RegData12
  Register #(.width(32)) Reg12 (.D(WrData), .en(WrReg12), .Q(RegData12), .clk(Clock));  // open: clr
  // Probe on RegData16
  Register #(.width(32)) Reg16 (.D(WrData), .en(WrReg16), .Q(RegData16), .clk(Clock));  // open: clr
  // Probe on RegData20
  Register #(.width(32)) Reg20 (.D(WrData), .en(WrReg20), .Q(RegData20), .clk(Clock));  // open: clr
  // Probe on RegData24
  Register #(.width(32)) Reg24 (.D(WrData), .en(WrReg24), .Q(RegData24), .clk(Clock));  // open: clr
  // Probe on RegData28
  Register #(.width(32)) Reg28 (.D(WrData), .en(WrReg28), .Q(RegData28), .clk(Clock));  // open: clr
  Register #(.width(32)) Reg1 (.D(WrData), .en(WrReg1), .Q(RegData1), .clk(Clock));  // open: clr
  Register #(.width(32)) Reg5 (.D(WrData), .en(WrReg5), .Q(RegData5), .clk(Clock));  // open: clr
  Register #(.width(32)) Reg9 (.D(WrData), .en(WrReg9), .Q(RegData9), .clk(Clock));  // open: clr
  Register #(.width(32)) Reg13 (.D(WrData), .en(WrReg13), .Q(RegData13), .clk(Clock));  // open: clr
  Register #(.width(32)) Reg17 (.D(WrData), .en(WrReg17), .Q(RegData17), .clk(Clock));  // open: clr
  Register #(.width(32)) Reg21 (.D(WrData), .en(WrReg21), .Q(RegData21), .clk(Clock));  // open: clr
  Register #(.width(32)) Reg25 (.D(WrData), .en(WrReg25), .Q(RegData25), .clk(Clock));  // open: clr
  Register #(.width(32)) Reg29 (.D(WrData), .en(WrReg29), .Q(RegData29), .clk(Clock));  // open: clr
  // Probe on RegData1
  // Probe on RegData5
  // Probe on RegData9
  // Probe on RegData13
  // Probe on RegData17
  // Probe on RegData21
  // Probe on RegData25
  // Probe on RegData29
  // Probe on RegData2
  Register #(.width(32)) Reg2 (.D(WrData), .en(WrReg2), .Q(RegData2), .clk(Clock));  // open: clr
  // Probe on RegData6
  Register #(.width(32)) Reg6 (.D(WrData), .en(WrReg6), .Q(RegData6), .clk(Clock));  // open: clr
  // Probe on RegData10
  Register #(.width(32)) Reg10 (.D(WrData), .en(WrReg10), .Q(RegData10), .clk(Clock));  // open: clr
  // Probe on RegData14
  Register #(.width(32)) Reg14 (.D(WrData), .en(WrReg14), .Q(RegData14), .clk(Clock));  // open: clr
  // Probe on RegData18
  Register #(.width(32)) Reg18 (.D(WrData), .en(WrReg18), .Q(RegData18), .clk(Clock));  // open: clr
  // Probe on RegData22
  Register #(.width(32)) Reg22 (.D(WrData), .en(WrReg22), .Q(RegData22), .clk(Clock));  // open: clr
  // Probe on RegData26
  Register #(.width(32)) Reg26 (.D(WrData), .en(WrReg26), .Q(RegData26), .clk(Clock));  // open: clr
  // Probe on RegData30
  Register #(.width(32)) Reg30 (.D(WrData), .en(WrReg30), .Q(RegData30), .clk(Clock));  // open: clr
  // Probe on RegData3
  Register #(.width(32)) Reg3 (.D(WrData), .en(WrReg3), .Q(RegData3), .clk(Clock));  // open: clr
  // Probe on RegData7
  Register #(.width(32)) Reg7 (.D(WrData), .en(WrReg7), .Q(RegData7), .clk(Clock));  // open: clr
  // Probe on RegData11
  Register #(.width(32)) Reg11 (.D(WrData), .en(WrReg11), .Q(RegData11), .clk(Clock));  // open: clr
  // Probe on RegData15
  Register #(.width(32)) Reg15 (.D(WrData), .en(WrReg15), .Q(RegData15), .clk(Clock));  // open: clr
  // Probe on RegData19
  Register #(.width(32)) Reg19 (.D(WrData), .en(WrReg19), .Q(RegData19), .clk(Clock));  // open: clr
  // Probe on RegData23
  Register #(.width(32)) Reg23 (.D(WrData), .en(WrReg23), .Q(RegData23), .clk(Clock));  // open: clr
  // Probe on RegData27
  Register #(.width(32)) Reg27 (.D(WrData), .en(WrReg27), .Q(RegData27), .clk(Clock));  // open: clr
  // Probe on RegData31
  Register #(.width(32)) Reg31 (.D(WrData), .en(WrReg31), .Q(RegData31), .clk(Clock));  // open: clr
  Multiplexer #(.select(5), .width(32), .enable("false")) multiplexer_1 (
    .in0({32{1'b0}}), .in1(RegData1), .in2(RegData2), .in3(RegData3), .in4(RegData4), .in5(RegData5),
    .in6(RegData6), .in7(RegData7), .in8(RegData8), .in9(RegData9), .in10(RegData10), .in11(RegData11),
    .in12(RegData12), .in13(RegData13), .in14(RegData14), .in15(RegData15), .in16(RegData16),
    .in17(RegData17), .in18(RegData18), .in19(RegData19), .in20(RegData20), .in21(RegData21),
    .in22(RegData22), .in23(RegData23), .in24(RegData24), .in25(RegData25), .in26(RegData26),
    .in27(RegData27), .in28(RegData28), .in29(RegData29), .in30(RegData30), .in31(RegData31),
    .out(multiplexer_1_out), .sel(RdAddr1));
  Multiplexer #(.select(5), .width(32), .enable("false")) multiplexer_2 (
    .in0({32{1'b0}}), .in1(RegData1), .in2(RegData2), .in3(RegData3), .in4(RegData4), .in5(RegData5),
    .in6(RegData6), .in7(RegData7), .in8(RegData8), .in9(RegData9), .in10(RegData10), .in11(RegData11),
    .in12(RegData12), .in13(RegData13), .in14(RegData14), .in15(RegData15), .in16(RegData16),
    .in17(RegData17), .in18(RegData18), .in19(RegData19), .in20(RegData20), .in21(RegData21),
    .in22(RegData22), .in23(RegData23), .in24(RegData24), .in25(RegData25), .in26(RegData26),
    .in27(RegData27), .in28(RegData28), .in29(RegData29), .in30(RegData30), .in31(RegData31),
    .out(multiplexer_2_out), .sel(RdAddr2));
  Multiplexer #(.width(32), .enable("false")) multiplexer_3 (
    .in0(multiplexer_1_out), .in1(WrData), .out(RdData1), .sel(and_1_out));
  Comparator #(.width(5), .mode("unsigned")) comparator_1 (
    .a(WrAddr), .b(RdAddr2), .eq(comparator_1_eq));  // open: gt, lt
  Multiplexer #(.width(32), .enable("false")) multiplexer_4 (
    .in0(multiplexer_2_out), .in1(WrData), .out(RdData2), .sel(and_2_out));
  Comparator #(.width(5), .mode("unsigned")) comparator_2 (
    .a(WrAddr), .b(RdAddr1), .eq(comparator_2_eq));  // open: gt, lt
  and and_1 (and_1_out, comparator_2_eq, WrReg, not_1_out);
  and and_2 (and_2_out, comparator_1_eq, WrReg, not_2_out);
  Comparator #(.width(5), .mode("unsigned")) comparator_3 (
    .a(WrAddr), .b({5{1'b0}}), .eq(comparator_3_eq));  // open: gt, lt
  not not_1 (not_1_out, comparator_3_eq);
  Comparator #(.width(5), .mode("unsigned")) comparator_4 (
    .a(WrAddr), .b({5{1'b0}}), .eq(comparator_4_eq));  // open: gt, lt
  not not_2 (not_2_out, comparator_4_eq);
endmodule

module Overflow_Unit (
  input  Add,
  input  Sub,
  input  ASign,
  input  BSign,
  input  ResultSign,
  output Overflow
);

  wire and_1_out, and_2_out, or_1_out, xnor_1_out, xor_1_out, xor_2_out;

  xnor xnor_1 (xnor_1_out, ASign, BSign);
  xor xor_1 (xor_1_out, ASign, BSign);
  and and_1 (and_1_out, xnor_1_out, Add);
  and and_2 (and_2_out, xor_1_out, Sub);
  or or_1 (or_1_out, and_1_out, and_2_out);
  xor xor_2 (xor_2_out, ResultSign, ASign);
  and and_3 (Overflow, or_1_out, xor_2_out);

  // Notes on the sheet:
  //   Overflow occurs when doing addition and sign(A) == sign(B) && sign(result) != sign(A)
  //   Or
  //   Overflow occurs when doing subtraction and sign(A) != sign(B) && sign(result) != sign(A)
endmodule

module IM (
  input  [7:0] Read_Address,
  input  Clock,
  output [31:0] Read_Data
);

  ROM #(.dataWidth(32)) rom_1 (.addr(Read_Address), .data(Read_Data));  // open: sel

  // Notes on the sheet:
  //   contents of rom_1 (hex, n*v repeats v):
  //   20010001 20020002 20030003 20040004 20050005 20060006 34270008 ac420012 434020 234824 a25022 665825
  //   c76026 c7682a 17280 27842 31500002 eb8827 8d920005
endmodule

module IF_ID (
  input  [31:0] PC_4,
  input  [31:0] Read_Address,
  input  Clock,
  input  IF_IDWrite,
  output [31:0] PC_4_Out,
  output [31:0] Read_Address_Out
);

  Register #(.width(32)) Address_PC_4 (.D(PC_4), .en(IF_IDWrite), .Q(PC_4_Out), .clk(Clock));  // open: clr
  Register #(.width(32)) u_Read_Address (
    .D(Read_Address), .en(IF_IDWrite), .Q(Read_Address_Out), .clk(Clock));  // open: clr

  // Other names for the same wires on the sheet: IF_Id_Write = IF_IDWrite
endmodule

module Control_Unit (
  input  Op5,
  input  Op4,
  input  Op3,
  input  Op2,
  input  Op1,
  input  Op0,
  input  in_7,
  output [1:0] RegDst,
  output ALUSrcB,
  output [1:0] MemtoReg,
  output RegWrite,
  output MemRead,
  output MemWrite,
  output PCWriteCond,
  output [1:0] PCSRC,
  output [2:0] ALUOP
);

  wire ADDI_out, ANDI_out, J_out, not_1_out, not_2_out, not_3_out, not_4_out, not_5_out, not_6_out,
       not_7_out, not_8_out, not_9_out, not_10_out, not_11_out, not_12_out, not_13_out, not_14_out,
       not_15_out, not_16_out, not_17_out, not_18_out, not_19_out, not_20_out, not_21_out, not_22_out,
       not_23_out, not_24_out, not_25_out, not_26_out, not_27_out, not_28_out, not_29_out, not_30_out,
       not_31_out, not_32_out, not_33_out, not_34_out, not_35_out, not_36_out, not_37_out, ORI_out;

  not not_1 (not_1_out, Op5);
  not not_2 (not_2_out, Op3);
  not not_3 (not_3_out, Op4);
  not not_4 (not_4_out, Op1);
  not not_5 (not_5_out, Op4);
  not not_6 (not_6_out, Op2);
  not not_7 (not_7_out, Op5);
  not not_8 (not_8_out, Op0);
  and R (ALUOP[2], not_1_out, not_3_out, not_2_out, in_7, not_6_out, not_4_out, not_8_out);
  not not_9 (not_9_out, Op0);
  not not_10 (not_10_out, Op1);
  not not_11 (not_11_out, Op4);
  not not_12 (not_12_out, Op5);
  and ANDI (ANDI_out, not_7_out, not_5_out, Op3, in_7, Op2, not_10_out, not_9_out);
  not not_13 (not_13_out, Op2);
  not not_14 (not_14_out, Op1);
  not not_15 (not_15_out, Op4);
  not not_16 (not_16_out, Op0);
  not not_17 (not_17_out, Op5);
  and ADDI (ADDI_out, not_12_out, not_11_out, Op3, in_7, not_13_out, not_14_out, not_16_out);
  not not_18 (not_18_out, Op3);
  not not_19 (not_19_out, Op1);
  not not_20 (not_20_out, Op4);
  and ORI (ORI_out, not_17_out, not_15_out, Op3, in_7, Op2, not_19_out, Op0);
  not not_21 (not_21_out, Op2);
  not not_22 (not_22_out, Op4);
  and LW (MemRead, Op5, not_20_out, not_18_out, in_7, not_21_out, Op1, Op0);
  not not_23 (not_23_out, Op5);
  not not_24 (not_24_out, Op4);
  not not_25 (not_25_out, Op3);
  not not_26 (not_26_out, Op2);
  and SW (MemWrite, Op5, not_22_out, Op3, in_7, not_26_out, Op1, Op0);
  not not_27 (not_27_out, Op0);
  not not_28 (not_28_out, Op5);
  not not_29 (not_29_out, Op4);
  not not_30 (not_30_out, Op3);
  not not_31 (not_31_out, Op1);
  and BEQ (PCSRC[0], not_23_out, not_24_out, not_25_out, in_7, Op2, not_31_out, not_27_out);
  not not_32 (not_32_out, Op5);
  not not_33 (not_33_out, Op2);
  not not_34 (not_34_out, Op4);
  not not_35 (not_35_out, Op3);
  not not_36 (not_36_out, Op0);
  and J (J_out, not_28_out, not_29_out, not_30_out, in_7, not_33_out, Op1, not_36_out);
  not not_37 (not_37_out, Op2);
  and JAL (MemtoReg[1], not_32_out, not_34_out, not_35_out, in_7, not_37_out, Op1, Op0);
  or or_1 (ALUSrcB, ANDI_out, ADDI_out, MemWrite, ORI_out, MemRead);
  or or_2 (PCSRC[1], J_out, MemtoReg[1]);
  or or_3 (RegWrite, ADDI_out, ALUOP[2], ANDI_out, ORI_out, MemRead, MemtoReg[1]);
  or or_4 (ALUOP[1], ANDI_out, ORI_out);
  or or_5 (ALUOP[0], PCSRC[0], ORI_out);

  assign MemtoReg[0] = MemRead;
  assign PCWriteCond = PCSRC[0];
  assign RegDst = {MemtoReg[1], ALUOP[2]};
endmodule

module ID_EX (
  input  [5:0] EX,
  input  [4:0] MEM,
  input  [2:0] WB,
  input  [31:0] PC_4,
  input  [31:0] ReadData1,
  input  [31:0] ReadData2,
  input  [31:0] SignExtend,
  input  [4:0] in_8,
  input  [4:0] in_9,
  input  [4:0] in_10,
  input  [31:0] in_11,
  input  Clock,
  output [1:0] RegDst,
  output ALUSrcB,
  output [2:0] ALUOp,
  output [4:0] out_16,
  output [2:0] out_17,
  output [31:0] PC_4_2,
  output [31:0] ReadData1_2,
  output [31:0] ReadData2_2,
  output [31:0] SignExtend_2,
  output [4:0] out_22,
  output [4:0] out_23,
  output [4:0] out_24,
  output [31:0] out_25
);

  wire [31:0] register_4_q;

  Register #(.width(6)) EXCtl (.D(EX), .Q({ALUOp, ALUSrcB, RegDst}), .clk(Clock));  // open: en, clr
  Register #(.width(5)) MEMCtl (.D(MEM), .Q(out_16), .clk(Clock));  // open: en, clr
  Register #(.width(3)) WBCTL (.D(WB), .Q(out_17), .clk(Clock));  // open: en, clr
  Register #(.width(32)) u_PC_4 (.D(PC_4), .Q(PC_4_2), .clk(Clock));  // open: en, clr
  Register #(.width(32)) u_ReadData1 (.D(ReadData1), .Q(ReadData1_2), .clk(Clock));  // open: en, clr
  Register #(.width(32)) u_ReadData2 (.D(ReadData2), .Q(ReadData2_2), .clk(Clock));  // open: en, clr
  Register #(.width(32)) Sign_Extend (.D(SignExtend), .Q(SignExtend_2), .clk(Clock));  // open: en, clr
  Register #(.width(5)) register_1 (.D(in_8), .Q(out_22), .clk(Clock));  // open: en, clr
  Register #(.width(5)) register_2 (.D(in_9), .Q(out_23), .clk(Clock));  // open: en, clr
  Register #(.width(5)) register_3 (.D(in_10), .Q(out_24), .clk(Clock));  // open: en, clr
  Register #(.width(32)) register_4 (.D(in_11), .Q(register_4_q), .clk(Clock));  // open: en, clr
  Register #(.width(32)) register_5 (.D(register_4_q), .Q(out_25), .clk(Clock));  // open: en, clr
endmodule

module ALUCTL (
  input  [5:0] Instr_5_0,
  input  [2:0] ALUOp,
  output [3:0] ToALU,
  output [1:0] JR
);

  wire and_1_out, and_2_out, and_3_out, and_4_out, and_5_out, and_6_out, and_7_out, and_8_out, and_9_out,
       and_10_out, and_11_out, and_12_out, and_13_out, and_14_out, and_15_out, and_17_out, not_1_out,
       not_2_out, not_3_out, not_4_out, not_5_out, not_6_out, not_7_out, not_8_out, not_9_out, not_10_out,
       not_11_out, not_12_out, not_13_out, not_14_out, not_15_out, not_16_out, not_17_out, not_18_out,
       not_19_out, not_20_out, not_21_out, not_22_out, not_23_out, not_24_out, not_25_out, not_26_out,
       not_27_out, not_28_out, not_29_out, not_30_out, not_31_out, not_32_out, not_33_out, not_34_out,
       not_35_out, not_36_out, not_37_out, not_38_out, not_39_out, not_40_out, not_41_out, not_42_out,
       not_43_out, not_44_out, not_45_out, not_46_out, not_47_out, not_48_out, not_49_out, not_50_out,
       not_51_out, not_52_out, not_53_out, not_54_out, not_55_out, not_56_out, not_57_out, not_58_out,
       not_59_out, not_60_out, or_1_out, or_2_out, or_3_out, or_4_out;

  not not_1 (not_1_out, Instr_5_0[4]);
  not not_2 (not_2_out, Instr_5_0[3]);
  not not_3 (not_3_out, Instr_5_0[0]);
  not not_4 (not_4_out, Instr_5_0[4]);
  not not_5 (not_5_out, Instr_5_0[3]);
  not not_6 (not_6_out, Instr_5_0[1]);
  not not_7 (not_7_out, Instr_5_0[5]);
  not not_8 (not_8_out, Instr_5_0[4]);
  not not_9 (not_9_out, Instr_5_0[3]);
  not not_10 (not_10_out, Instr_5_0[2]);
  not not_11 (not_11_out, Instr_5_0[0]);
  not not_12 (not_12_out, Instr_5_0[4]);
  not not_13 (not_13_out, Instr_5_0[3]);
  not not_14 (not_14_out, Instr_5_0[1]);
  not not_15 (not_15_out, Instr_5_0[4]);
  not not_16 (not_16_out, Instr_5_0[2]);
  not not_17 (not_17_out, Instr_5_0[0]);
  not not_18 (not_18_out, Instr_5_0[5]);
  not not_19 (not_19_out, Instr_5_0[4]);
  not not_20 (not_20_out, Instr_5_0[3]);
  not not_21 (not_21_out, Instr_5_0[2]);
  not not_22 (not_22_out, Instr_5_0[0]);
  not not_23 (not_23_out, Instr_5_0[5]);
  not not_24 (not_24_out, Instr_5_0[4]);
  not not_25 (not_25_out, Instr_5_0[3]);
  not not_26 (not_26_out, Instr_5_0[2]);
  not not_27 (not_27_out, Instr_5_0[1]);
  not not_28 (not_28_out, Instr_5_0[0]);
  not not_29 (not_29_out, Instr_5_0[4]);
  not not_30 (not_30_out, Instr_5_0[3]);
  not not_31 (not_31_out, Instr_5_0[4]);
  not not_32 (not_32_out, Instr_5_0[2]);
  not not_33 (not_33_out, Instr_5_0[0]);
  not not_34 (not_34_out, Instr_5_0[5]);
  not not_35 (not_35_out, Instr_5_0[4]);
  not not_36 (not_36_out, Instr_5_0[3]);
  not not_37 (not_37_out, Instr_5_0[2]);
  not not_38 (not_38_out, Instr_5_0[0]);
  not not_39 (not_39_out, Instr_5_0[5]);
  not not_40 (not_40_out, Instr_5_0[4]);
  not not_41 (not_41_out, Instr_5_0[3]);
  not not_42 (not_42_out, Instr_5_0[2]);
  not not_43 (not_43_out, Instr_5_0[1]);
  not not_44 (not_44_out, Instr_5_0[0]);
  not not_45 (not_45_out, Instr_5_0[5]);
  not not_46 (not_46_out, Instr_5_0[4]);
  not not_47 (not_47_out, Instr_5_0[3]);
  not not_48 (not_48_out, Instr_5_0[2]);
  not not_49 (not_49_out, Instr_5_0[0]);
  not not_50 (not_50_out, Instr_5_0[5]);
  not not_51 (not_51_out, Instr_5_0[4]);
  not not_52 (not_52_out, Instr_5_0[3]);
  not not_53 (not_53_out, Instr_5_0[2]);
  not not_54 (not_54_out, Instr_5_0[1]);
  not not_55 (not_55_out, Instr_5_0[0]);
  not not_56 (not_56_out, Instr_5_0[5]);
  not not_57 (not_57_out, Instr_5_0[4]);
  not not_58 (not_58_out, Instr_5_0[2]);
  not not_59 (not_59_out, Instr_5_0[1]);
  not not_60 (not_60_out, Instr_5_0[0]);
  and and_1 (and_1_out, Instr_5_0[5], not_1_out, not_2_out, Instr_5_0[1], not_3_out);
  and and_2 (and_2_out, Instr_5_0[5], not_4_out, not_5_out, Instr_5_0[2], not_6_out, Instr_5_0[0]);
  and and_3 (and_3_out, not_7_out, not_8_out, not_9_out, not_10_out, Instr_5_0[1], not_11_out);
  and and_4 (and_4_out, Instr_5_0[5], not_12_out, not_13_out, Instr_5_0[2], not_14_out);
  and and_5 (and_5_out, Instr_5_0[5], not_15_out, Instr_5_0[3], not_16_out, Instr_5_0[1], not_17_out);
  and and_6 (and_6_out, not_18_out, not_19_out, not_20_out, not_21_out, Instr_5_0[1], not_22_out);
  and and_7 (and_7_out, not_23_out, not_24_out, not_25_out, not_26_out, not_27_out, not_28_out);
  and and_8 (and_8_out, Instr_5_0[5], not_29_out, not_30_out, Instr_5_0[2], Instr_5_0[1]);
  and and_9 (and_9_out, Instr_5_0[5], not_31_out, Instr_5_0[3], not_32_out, Instr_5_0[1], not_33_out);
  and and_10 (and_10_out, not_34_out, not_35_out, not_36_out, not_37_out, Instr_5_0[1], not_38_out);
  and and_11 (and_11_out, not_39_out, not_40_out, not_41_out, not_42_out, not_43_out, not_44_out);
  and and_12 (and_12_out, not_45_out, not_46_out, not_47_out, not_48_out, Instr_5_0[1], not_49_out);
  and and_13 (and_13_out, not_50_out, not_51_out, not_52_out, not_53_out, not_54_out, not_55_out);
  and and_14 (and_14_out, not_56_out, not_57_out, Instr_5_0[3], not_58_out, not_59_out, not_60_out, ALUOp[2]);
  and and_15 (and_15_out, ALUOp[2], or_1_out);
  or or_1 (or_1_out, and_1_out, and_2_out, and_3_out);
  or or_2 (or_2_out, and_4_out, and_5_out, and_6_out, and_7_out);
  or or_3 (or_3_out, and_8_out, and_9_out, and_10_out, and_11_out);
  and and_16 (ToALU[3], ALUOp[2], or_4_out);
  or or_4 (or_4_out, and_12_out, and_13_out);
  Multiplexer #(.width(2), .enable("false")) multiplexer_1 (.in0(2'b00), .in1(2'b11), .out(JR), .sel(and_14_out));
  or or_5 (ToALU[0], and_15_out, ALUOp[0]);
  and and_17 (and_17_out, ALUOp[2], or_2_out);
  or or_6 (ToALU[1], and_17_out, ALUOp[1]);
  and and_18 (ToALU[2], ALUOp[2], or_3_out);
endmodule

module EX_MEM (
  input  [2:0] WB,
  input  [4:0] M,
  input  [31:0] Add_Result,
  input  ALU_Zero,
  input  [31:0] ALU_Result,
  input  [31:0] Read_Data_2,
  input  [4:0] Instruction,
  input  Clock,
  output [2:0] WB_Out,
  output [1:0] PCSrc,
  output MemRead,
  output MemWrite,
  output Branch,
  output [31:0] Add_Result_Out,
  output ALU_Zero_Out,
  output [31:0] ALU_Result_Out,
  output [31:0] Read_Data_2_Out,
  output [4:0] Instruction_Out
);

  Register #(.width(3)) register_1 (.D(WB), .Q(WB_Out), .clk(Clock));  // open: en, clr
  Register #(.width(5)) register_2 (.D(M), .Q({Branch, MemWrite, MemRead, PCSrc}), .clk(Clock));  // open: en, clr
  Register #(.width(32)) register_3 (.D(Add_Result), .Q(Add_Result_Out), .clk(Clock));  // open: en, clr
  Register #(.width(1)) register_4 (.D(ALU_Zero), .Q(ALU_Zero_Out), .clk(Clock));  // open: en, clr
  Register #(.width(32)) register_5 (.D(ALU_Result), .Q(ALU_Result_Out), .clk(Clock));  // open: en, clr
  Register #(.width(32)) register_6 (.D(Read_Data_2), .Q(Read_Data_2_Out), .clk(Clock));  // open: en, clr
  Register #(.width(5)) register_7 (.D(Instruction), .Q(Instruction_Out), .clk(Clock));  // open: en, clr
endmodule

module DM (
  input  [7:0] Address,
  input  [31:0] Write_Data,
  input  MemWrite,
  input  Clock,
  input  MemRead,
  output [31:0] Read_Data
);

  RAM #(.dataWidth(32), .bus("separate")) ram_1 (
    .addr(Address), .din(Write_Data), .data(Read_Data), .str(MemWrite), .clk(Clock), .ld(MemRead));  // open: sel, clr
endmodule

module MEM_WB (
  input  [2:0] WB,
  input  [31:0] Read_Data,
  input  [31:0] Write_Address,
  input  [4:0] Reg_Address,
  input  Clock,
  output [1:0] MemToReg,
  output RegWrite,
  output [31:0] Read_Data_Out,
  output [31:0] Write_Address_Out,
  output [4:0] Reg_AddressOut
);

  Register #(.width(3)) register_1 (.D(WB), .Q({RegWrite, MemToReg}), .clk(Clock));  // open: en, clr
  Register #(.width(32)) register_2 (.D(Read_Data), .Q(Read_Data_Out), .clk(Clock));  // open: en, clr
  Register #(.width(32)) register_3 (.D(Write_Address), .Q(Write_Address_Out), .clk(Clock));  // open: en, clr
  Register #(.width(5)) register_4 (.D(Reg_Address), .Q(Reg_AddressOut), .clk(Clock));  // open: en, clr
endmodule

module Mini_5_1 (
  input  [4:0] in_1,
  output out_2
);

  Decoder #(.select(5), .enable("false")) decoder_1 (
    .out0(out_2), .sel(in_1));  // open: out1, out2, out3, out4, out5, out6, out7, out8, out9, out10, out11, out12, out13, out14, out15, out16, out17, out18, out19, out20, out21, out22, out23, out24, out25, out26, out27, out28, out29, out30, out31
endmodule

module Forwarding_Unit (
  input  RegWrite_Mem,
  input  RegWrite_WB,
  input  [4:0] rd_MEM,
  input  [4:0] rd_WB,
  input  [4:0] rd_EX,
  input  [4:0] rs_EX,
  output Forwad_B_MEM,
  output Forward_B_WB,
  output Forward_A_Mem,
  output Forward_A_WB
);

  wire comparator_1_eq, comparator_2_eq, comparator_3_eq, comparator_4_eq, comparator_5_eq, comparator_6_eq,
       comparator_7_eq, comparator_8_eq, not_1_out, not_2_out, not_3_out, not_4_out, not_5_out, not_6_out;

  Comparator #(.width(5)) comparator_1 (.a({5{1'b0}}), .b(rd_EX), .eq(comparator_1_eq));  // open: gt, lt
  Comparator #(.width(5)) comparator_2 (.a({5{1'b0}}), .b(rs_EX), .eq(comparator_2_eq));  // open: gt, lt
  Comparator #(.width(5)) comparator_3 (.a(rd_MEM), .b(rd_EX), .eq(comparator_3_eq));  // open: gt, lt
  not not_1 (not_1_out, comparator_1_eq);
  Comparator #(.width(5)) comparator_4 (.a(rd_MEM), .b(rs_EX), .eq(comparator_4_eq));  // open: gt, lt
  not not_2 (not_2_out, comparator_2_eq);
  and and_1 (Forwad_B_MEM, RegWrite_Mem, comparator_3_eq, not_1_out);
  and and_2 (Forward_A_Mem, RegWrite_Mem, comparator_4_eq, not_2_out);
  Comparator #(.width(5)) comparator_5 (.a(rd_WB), .b(rd_EX), .eq(comparator_5_eq));  // open: gt, lt
  Comparator #(.width(5)) comparator_6 (.a({5{1'b0}}), .b(rd_EX), .eq(comparator_6_eq));  // open: gt, lt
  Comparator #(.width(5)) comparator_7 (.a(rd_WB), .b(rs_EX), .eq(comparator_7_eq));  // open: gt, lt
  Comparator #(.width(5)) comparator_8 (.a({5{1'b0}}), .b(rs_EX), .eq(comparator_8_eq));  // open: gt, lt
  not not_3 (not_3_out, comparator_6_eq);
  not not_4 (not_4_out, comparator_8_eq);
  not not_5 (not_5_out, Forwad_B_MEM);
  and and_3 (Forward_B_WB, not_5_out, RegWrite_WB, comparator_5_eq, not_3_out);
  not not_6 (not_6_out, Forward_A_Mem);
  and and_4 (Forward_A_WB, not_6_out, RegWrite_WB, comparator_7_eq, not_4_out);
endmodule

module sub (
  input  [31:0] in_1,
  output out_2
);

  and and_1 (out_2, in_1[0], in_1[1], in_1[2], in_1[3], in_1[4], in_1[5], in_1[6], in_1[7], in_1[8], in_1[9], in_1[10], in_1[11], in_1[12], in_1[13], in_1[14], in_1[15], in_1[17], in_1[18], in_1[19], in_1[20], in_1[21], in_1[22], in_1[23], in_1[24], in_1[25], in_1[26], in_1[27], in_1[28], in_1[29], in_1[30], in_1[31], in_1[16]);
endmodule

module Hazard_Detection (
  input  MemRead,
  input  [4:0] ID_EX_Register_Rt,
  input  [4:0] IF_ID_RegisterRs,
  input  [4:0] IF_ID_RegisterRt,
  output PCWrite,
  output IF_IDWrite,
  output ControlWrite
);

  wire and_1_out, comparator_1_eq, comparator_2_eq, comparator_3_eq, not_1_out, or_1_out;

  Comparator #(.width(5)) comparator_1 (.a(ID_EX_Register_Rt), .b({5{1'b0}}), .eq(comparator_1_eq));  // open: gt, lt
  Comparator #(.width(5)) comparator_2 (
    .a(ID_EX_Register_Rt), .b(IF_ID_RegisterRs), .eq(comparator_2_eq));  // open: gt, lt
  Comparator #(.width(5)) comparator_3 (
    .a(ID_EX_Register_Rt), .b(IF_ID_RegisterRt), .eq(comparator_3_eq));  // open: gt, lt
  not not_1 (not_1_out, comparator_1_eq);
  or or_1 (or_1_out, comparator_2_eq, comparator_3_eq);
  and and_1 (and_1_out, MemRead, not_1_out, or_1_out);
  buf or_2 (ControlWrite, and_1_out);  // OR_Gate

  assign IF_IDWrite = ControlWrite;
  assign PCWrite = ControlWrite;
endmodule
